# Fritzing sketch GPIOSketch (saved by Fritzing 0.9.5d)
breadboards: 2

parts:
  Part1 = Adafruit Audio FX Mini Sound Board [part_number="Adafruit #2342 and #2220"]
  Part2 = Arduino Uno (Rev3)
  S1 = Pushbutton [package="[THT]"]
  S2 = Pushbutton [package="[THT]"]
  S3 = Pushbutton [package="[THT]"]
  S4 = Pushbutton [package="[THT]"]
  S5 = Pushbutton [package="[THT]"]
  J2 = Generic female header - 6 pins [form="♀ (female)" package=THT]
  SP1 = SPEAKER [package=pcb_mount_speaker]
  BATT1 = 4xAA Switchable Battery Pack w/Bare Wire

nets:
  GND: Part1.GND, Part2.GND, S1.Pin_3, S1.Pin_4, S2.Pin_3, S2.Pin_4, S3.Pin_3, S3.Pin_4, S4.Pin_3, S4.Pin_4, S5.Pin_3, S5.Pin_4, J2.-ve_Input
  N1: Part1.GPIO0_4, S5.Pin_1, S5.Pin_2
  N2: Part1.GPIO0_3, S4.Pin_1, S4.Pin_2
  N3: Part1.GPIO0_2, S3.Pin_1, S3.Pin_2
  N4: Part1.GPIO0_1, S2.Pin_1, S2.Pin_2
  N5: Part1.GPIO0_0, S1.Pin_1, S1.Pin_2
  VIN: Part1.VIN, Part2.5V
  N6: Part1.L_AC, J2.+ve_Input
  N7: J2.-ve_VCC, BATT1.NEG
  N8: J2.+ve_VCC, BATT1.POS
  N9: J2.+ve_Output, SP1.-
  N10: J2.-ve_Output, SP1.+

notes:
  -ve
  +ve
  12V
  Arduino Uno
  TPA3116D2 Mono 100W
  PYLE PL42BL
  Adafruit Audio FX Mini Sound Board

custom parts:
  Adafruit Audio FX Mini Sound Board: Would you like to add audio/sound effects to your next project, without an Arduino+Shield? Or maybe you don't even know how to use microcontrollers, you just want to make a sound play whenever you press a button. What about something that has to be very small and portable? You are probably feeling a little frustrated: it's been very hard to find a simple, low cost audio effects trigger that is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
  Generic female header - 6 pins: Generic female header
  4xAA Switchable Battery Pack w/Bare Wire: 4xAA Switchable Battery Pack with Bare Wire connection
